# Fritzing sketch Tag_04 (saved by Fritzing 1.0.6)
breadboards: 1

parts:
  MCU1 = Raspberry Pi Zero
  R1 = Resistor [tolerance=±5% power=0.25W resistance=220 package=THT]
  LED1 = LED - 5mm [color="Red (633nm)" current=0.030A package="5 mm [THT]"]

nets:
  N1: MCU1.pin_6, MCU1.pin_9, LED1.cathode
  N2: MCU1.pin_11, R1.Pin_1
  N3: R1.Pin_0, LED1.anode
